# Fritzing sketch fog_machine (saved by Fritzing 0.9.4)

parts:
  Composant1 = Arduino Uno (Rev3)  # not connected
  Composant2 = Arduino Ethernet Shield (Rev3)
  U1 = 2-Channel 5v Relay Shield [package=relay-2ch5v10a]

nets:
  N1: Composant2.A0, U1.IN2
  N2: Composant2.A1, U1.IN1
  5V: Composant2.5V, U1.VCC
  GND: Composant2.GND, U1.GND

notes:
  Ethernet Shield mounted on Arduino uno
  Fog machine power cord hack
  Fog machine remote control hack

custom parts:
  2-Channel 5v Relay Shield: 2 Channel 5v Relay Shield w. 2x SPD-06VDC-SD-C
